// Logisim project 8bit-cpu.circ as structural Verilog: 7 circuits, main circuit main
module main (
  input  in_1,
  input  in_2,
  input  in_3,
  input  in_4,
  output out_5,
  output out_6
);

  wire and_1_out, clock_1_out, clock_2_out, clock_3_out, clock_4_out, controlunit_module_1_out_en,
       controlunit_module_1_pc_load, controlunit_module_1_wreg_we, undriven;
  wire [7:0] adder_1_out, controlled_buffer_1_out, multiplexer_1_out, PC_q;
  wire [12:0] rom_module_1_data;

  Adder adder_1 (.a(PC_q), .b(8'h1), .out(adder_1_out));  // open: cin, cout
  Multiplexer #(.width(8)) multiplexer_1 (
    .in0(adder_1_out), .in1(PC_q), .out(multiplexer_1_out), .sel(controlunit_module_1_out_en));
  Clock clock_1 (.out(clock_1_out));
  Multiplexer multiplexer_2 (.in0(in_2), .in1(in_3), .out(out_6), .sel(in_4));
  Register PC (.D(multiplexer_1_out), .clk(clock_2_out), .Q(PC_q));  // open: en, clr
  Clock clock_2 (.out(clock_2_out));
  Register #(.width(1)) register_1 (.D(in_1), .en(undriven), .clk(clock_1_out), .Q(out_5));  // open: clr
  ROM_module rom_module_1 (.addr(PC_q), .data(rom_module_1_data));
  and and_1 (and_1_out, clock_3_out, controlunit_module_1_pc_load);
  Clock clock_3 (.out(clock_3_out));
  assign controlled_buffer_1_out = and_1_out ? rom_module_1_data[7:0] : 8'bz;  // Controlled_Buffer controlled_buffer_1
  ControlUnit_module controlunit_module_1 (
    .operand(controlled_buffer_1_out), .opcode(rom_module_1_data[12:8]),
    .Wreg_WE(controlunit_module_1_wreg_we), .PC_LOAD(controlunit_module_1_pc_load),
    .OUT_EN(controlunit_module_1_out_en), .HALT(controlunit_module_1_out_en));  // open: zeroF, carryF, WREG_RE, REG_WE, REG_SEL, RAM_RE, RAM_WE, RAM_ADDR_EN, ALU_OP, ALU_EN, PC_EN, ROM_TO_DATABUS, RN_TO_DATABUS, IN_TO_DATABUS
  Register Wreg (.en(controlunit_module_1_wreg_we), .clk(clock_4_out));  // open: D, Q, clr
  Clock clock_4 (.out(clock_4_out));

  // Notes on the sheet:
  //   DATABUS
endmodule

module ALU (
  input  ALUOP2,
  input  ALUOP1,
  input  ALUOP0,
  input  [7:0] Wreg,
  input  [7:0] Rn,
  output [7:0] Result,
  output carryF,
  output zeroF
);

  wire and_2_out, and_3_out, and_4_out, not_3_out, not_4_out, xor_2_out;
  wire [7:0] adder_1_out, adder_2_out, and_1_out, multiplexer_1_out, multiplexer_2_out, multiplexer_3_out,
       multiplexer_4_out, not_1_out, not_2_out, or_1_out, xor_1_out;

  assign not_1_out = ~Wreg;  // NOT_Gate not_1, 8 bits wide
  Adder adder_1 (.a(8'h1), .b(not_2_out), .out(adder_1_out));  // open: cin, cout
  assign not_2_out = ~Rn;  // NOT_Gate not_2, 8 bits wide
  assign and_1_out = Wreg & Rn;  // AND_Gate and_1, 8 bits wide
  assign or_1_out = Wreg | Rn;  // OR_Gate or_1, 8 bits wide
  assign xor_1_out = Wreg ^ Rn;  // XOR_Gate xor_1, 8 bits wide
  and and_2 (and_2_out, ALUOP1, ALUOP2);
  Multiplexer #(.width(8)) multiplexer_1 (.in0(Rn), .in1(adder_1_out), .out(multiplexer_1_out), .sel(ALUOP0));
  Multiplexer #(.width(8)) multiplexer_2 (.in0(8'h1), .in1({8{1'b1}}), .out(multiplexer_2_out), .sel(ALUOP0));
  Multiplexer #(.width(8)) multiplexer_3 (
    .in0(multiplexer_1_out), .in1(multiplexer_2_out), .out(multiplexer_3_out), .sel(and_2_out));
  not not_3 (not_3_out, ALUOP1);
  not not_4 (not_4_out, ALUOP2);
  Adder adder_2 (.a(Wreg), .b(multiplexer_3_out), .out(adder_2_out), .cout(carryF));  // open: cin
  and and_3 (and_3_out, not_3_out, ALUOP2);
  and and_4 (and_4_out, ALUOP1, not_4_out);
  xor xor_2 (xor_2_out, and_3_out, and_4_out);
  Multiplexer #(.select(3), .width(8)) multiplexer_4 (
    .in2(and_1_out), .in3(or_1_out), .in4(xor_1_out), .in5(not_1_out), .out(multiplexer_4_out),
    .sel({ALUOP2, ALUOP1, ALUOP0}));  // open: in0, in1, in6, in7
  Multiplexer #(.width(8)) multiplexer_5 (.in0(adder_2_out), .in1(multiplexer_4_out), .out(Result), .sel(xor_2_out));
  Comparator comparator_1 (.a({8{1'b0}}), .b(adder_2_out), .eq(zeroF));  // open: gt, lt
endmodule

module ROM_module (
  input  [7:0] addr,
  output [12:0] data
);

  ROM #(.dataWidth(13)) rom_1 (.addr(addr), .data(data));

  // Notes on the sheet:
  //   contents of rom_1 (hex, n*v repeats v):
  //   155 1501 1004 155 1502 1007 155 1504 100a 155 1508 100d 155 1510 1010 155 1520 1013 155 1540 1016
  //   155 1580 1000
endmodule

module RAM_module (
  input  [7:0] addr,
  input  [7:0] dataIn,
  input  readEnable,
  input  writeEnable,
  input  clk,
  output [7:0] dataOut
);

  wire [7:0] ram_1_dout;

  RAM #(.asyncread("true")) ram_1 (
    .addr(addr), .we(writeEnable), .oe(readEnable), .clk(clk), .din(dataIn), .dout(ram_1_dout));
  assign dataOut = readEnable ? ram_1_dout : 8'bz;  // Controlled_Buffer controlled_buffer_1
endmodule

module Registers_Module (
  input  [2:0] readSelect,
  input  [7:0] dataIn,
  input  clk,
  input  clear,
  input  [2:0] writeSelect,
  input  writeEnable,
  output [7:0] dataOut
);

  wire decoder_1_out0, decoder_1_out1, decoder_1_out2, decoder_1_out3, decoder_1_out4, decoder_1_out5,
       decoder_1_out6, decoder_1_out7;
  wire [7:0] MA_q, MD_q, R0_q, R1_q, R2_q, R3_q, SP_q, Wreg_q;

  Decoder #(.select(3)) decoder_1 (
    .out0(decoder_1_out0), .out1(decoder_1_out1), .out2(decoder_1_out2), .out3(decoder_1_out3),
    .out4(decoder_1_out4), .out5(decoder_1_out5), .out6(decoder_1_out6), .out7(decoder_1_out7),
    .sel(writeSelect), .en(writeEnable));
  Register Wreg (.D(dataIn), .en(decoder_1_out0), .clk(clk), .Q(Wreg_q), .clr(clear));
  Register R0 (.D(dataIn), .en(decoder_1_out1), .clk(clk), .Q(R0_q), .clr(clear));
  Register R1 (.D(dataIn), .en(decoder_1_out2), .clk(clk), .Q(R1_q), .clr(clear));
  Register R2 (.D(dataIn), .en(decoder_1_out3), .clk(clk), .Q(R2_q), .clr(clear));
  Register R3 (.D(dataIn), .en(decoder_1_out4), .clk(clk), .Q(R3_q), .clr(clear));
  Register SP (.D(dataIn), .en(decoder_1_out5), .clk(clk), .Q(SP_q), .clr(clear));
  Register MD (.D(dataIn), .en(decoder_1_out6), .clk(clk), .Q(MD_q), .clr(clear));
  Register MA (.D(dataIn), .en(decoder_1_out7), .clk(clk), .Q(MA_q), .clr(clear));
  Multiplexer #(.select(3), .width(8)) multiplexer_1 (
    .in0(Wreg_q), .in1(R0_q), .in2(R1_q), .in3(R2_q), .in4(R3_q), .in5(SP_q), .in6(MD_q), .in7(MA_q),
    .out(dataOut), .sel(readSelect));
endmodule

module ControlUnit_module (
  input  [7:0] operand,
  input  [4:0] opcode,
  input  zeroF,
  input  carryF,
  output Wreg_WE,
  output WREG_RE,
  output REG_WE,
  output [2:0] REG_SEL,
  output RAM_RE,
  output RAM_WE,
  output RAM_ADDR_EN,
  output [2:0] ALU_OP,
  output ALU_EN,
  output PC_LOAD,
  output PC_EN,
  output ROM_TO_DATABUS,
  output RN_TO_DATABUS,
  output IN_TO_DATABUS,
  output OUT_EN,
  output HALT
);

  wire and_1_out, and_2_out, data_out, decoder_1_out0, decoder_1_out1, decoder_1_out6, decoder_1_out7,
       decoder_1_out8, decoder_1_out9, decoder_1_out10, decoder_1_out11, decoder_1_out12, decoder_1_out13,
       decoder_1_out14, decoder_1_out15, decoder_1_out16, decoder_1_out17, decoder_1_out18, not_1_out,
       not_2_out, not_3_out, or_1_out, or_2_out, or_3_out, or_4_out, or_5_out, or_6_out, or_8_out, or_10_out,
       or_11_out, or_12_out, or_14_out, or_15_out;

  Decoder #(.select(5)) decoder_1 (
    .out0(decoder_1_out0), .out1(decoder_1_out1), .out2(RAM_RE), .out3(RAM_WE), .out4(RN_TO_DATABUS),
    .out5(REG_WE), .out6(decoder_1_out6), .out7(decoder_1_out7), .out8(decoder_1_out8),
    .out9(decoder_1_out9), .out10(decoder_1_out10), .out11(decoder_1_out11), .out12(decoder_1_out12),
    .out13(decoder_1_out13), .out14(decoder_1_out14), .out15(decoder_1_out15), .out16(decoder_1_out16),
    .out17(decoder_1_out17), .out18(decoder_1_out18), .out19(HALT), .out20(IN_TO_DATABUS), .out21(OUT_EN),
    .sel(opcode));  // open: out22, out23, out24, out25, out26, out27, out28, out29, out30, out31, en
  not not_1 (not_1_out, opcode[4]);
  not not_2 (not_2_out, opcode[3]);
  not not_3 (not_3_out, opcode[4]);
  and ALU (ALU_EN, opcode[3], not_1_out);
  and data (data_out, not_2_out, not_3_out);
  or or_1 (or_1_out, decoder_1_out9, decoder_1_out10);
  or or_2 (or_2_out, decoder_1_out11, decoder_1_out12);
  or or_3 (or_3_out, RN_TO_DATABUS, REG_WE);
  or or_4 (or_4_out, or_1_out, or_2_out);
  or or_5 (or_5_out, decoder_1_out8, or_4_out);
  and and_1 (and_1_out, decoder_1_out17, zeroF);
  and and_2 (and_2_out, decoder_1_out18, carryF);
  or or_6 (or_6_out, or_3_out, or_5_out);
  or or_7 (RAM_ADDR_EN, RAM_RE, RAM_WE);
  or or_8 (or_8_out, and_1_out, and_2_out);
  assign REG_SEL = or_6_out ? operand[2:0] : 3'bz;  // Controlled_Buffer rn_address
  or or_9 (PC_LOAD, decoder_1_out16, or_8_out);
  or or_10 (or_10_out, RAM_WE, REG_WE);
  or or_11 (or_11_out, decoder_1_out1, RAM_RE);
  or or_12 (or_12_out, RN_TO_DATABUS, decoder_1_out7);
  or or_13 (WREG_RE, or_10_out, decoder_1_out6);
  or or_14 (or_14_out, or_11_out, or_12_out);
  or or_15 (or_15_out, or_14_out, ALU_EN);
  or or_16 (PC_EN, ALU_EN, data_out);
  or or_17 (Wreg_WE, IN_TO_DATABUS, or_15_out);
  or or_18 (ROM_TO_DATABUS, PC_LOAD, decoder_1_out1);

  assign ALU_OP = opcode[2:0];

  // Notes on the sheet:
  //   Rn address bus
  //   SUB
  //   AND
  //   OR
  //   XOR
  //   NOT
  //   INC
  //   DEC
  //   JMP
  //   JZ
  //   JC
  //   STORE
  //   CLEAR
  //   ADD
  //   HALT
  //   LOADI
  //   LOADA
  //   MOV
  //   MOVW
  //   SET
  //   NOP
endmodule

module Computer (
  output [7:0] out_1,
  output [7:0] out_2,
  output [7:0] out_3,
  output [7:0] out_4,
  output [6:0] out_5
);

  wire alu_1_carryf, alu_1_zerof, and_1_out, clock_1_out, clock_2_out, clock_3_out, clock_4_out, clock_5_out,
       clock_6_out, clock_7_out, controlled_buffer_5_out, controlunit_module_1_alu_en,
       controlunit_module_1_halt, controlunit_module_1_in_to_databus, controlunit_module_1_out_en,
       controlunit_module_1_pc_en, controlunit_module_1_pc_load, controlunit_module_1_ram_addr_en,
       controlunit_module_1_ram_re, controlunit_module_1_ram_we, controlunit_module_1_reg_we,
       controlunit_module_1_rn_to_databus, controlunit_module_1_rom_to_databus, controlunit_module_1_wreg_re,
       controlunit_module_1_wreg_we, d_ff_1_q, d_ff_2_q, keyboard_1_avail, not_1_out;
  wire [2:0] controlunit_module_1_alu_op, controlunit_module_1_reg_sel;
  wire [7:0] adder_1_out, alu_1_result, controlled_buffer_1_out, controlled_buffer_3_out,
       controlled_buffer_7_out, key_q, multiplexer_1_out, PC_q, register_1_q, register_2_q,
       registers_module_1_dataout, ROM_TO_DATABUS_out;
  wire [12:0] rom_module_1_data;

  Adder adder_1 (.a(PC_q), .b(8'h1), .out(adder_1_out));  // open: cin, cout
  assign controlled_buffer_1_out = controlunit_module_1_pc_load ? rom_module_1_data[7:0] : 8'bz;  // Controlled_Buffer controlled_buffer_1
  not not_1 (not_1_out, controlunit_module_1_pc_load);
  assign controlled_buffer_1_out = not_1_out ? multiplexer_1_out : 8'bz;  // Controlled_Buffer controlled_buffer_2
  Multiplexer #(.width(8)) multiplexer_1 (
    .in0(adder_1_out), .in1(PC_q), .out(multiplexer_1_out), .sel(controlunit_module_1_halt));
  Clock clock_1 (.out(clock_1_out));
  Register PC (.D(controlled_buffer_1_out), .clk(clock_1_out), .Q(PC_q));  // open: en, clr
  ROM_module rom_module_1 (.addr(PC_q), .data(rom_module_1_data));
  and and_1 (and_1_out, clock_2_out, controlunit_module_1_pc_en);
  Clock clock_2 (.out(clock_2_out));
  assign controlled_buffer_3_out = and_1_out ? rom_module_1_data[7:0] : 8'bz;  // Controlled_Buffer controlled_buffer_3
  assign ROM_TO_DATABUS_out = controlunit_module_1_rom_to_databus ? rom_module_1_data[7:0] : 8'bz;  // Controlled_Buffer ROM_TO_DATABUS
  ControlUnit_module controlunit_module_1 (
    .operand(controlled_buffer_3_out), .opcode(rom_module_1_data[12:8]), .zeroF(d_ff_2_q), .carryF(d_ff_1_q),
    .Wreg_WE(controlunit_module_1_wreg_we), .WREG_RE(controlunit_module_1_wreg_re),
    .REG_WE(controlunit_module_1_reg_we), .REG_SEL(controlunit_module_1_reg_sel),
    .RAM_RE(controlunit_module_1_ram_re), .RAM_WE(controlunit_module_1_ram_we),
    .RAM_ADDR_EN(controlunit_module_1_ram_addr_en), .ALU_OP(controlunit_module_1_alu_op),
    .ALU_EN(controlunit_module_1_alu_en), .PC_LOAD(controlunit_module_1_pc_load),
    .PC_EN(controlunit_module_1_pc_en), .ROM_TO_DATABUS(controlunit_module_1_rom_to_databus),
    .RN_TO_DATABUS(controlunit_module_1_rn_to_databus), .IN_TO_DATABUS(controlunit_module_1_in_to_databus),
    .OUT_EN(controlunit_module_1_out_en), .HALT(controlunit_module_1_halt));
  Clock clock_3 (.out(clock_3_out));
  assign out_2 = controlunit_module_1_ram_addr_en ? rom_module_1_data[7:0] : 8'bz;  // Controlled_Buffer controlled_buffer_4
  Register Wreg (.D(ROM_TO_DATABUS_out), .en(controlunit_module_1_wreg_we), .clk(clock_4_out), .Q(out_3));  // open: clr
  Clock clock_4 (.out(clock_4_out));
  Registers_Module registers_module_1 (
    .readSelect(controlunit_module_1_reg_sel), .dataIn(out_3), .clk(clock_3_out),
    .writeSelect(controlunit_module_1_reg_sel), .writeEnable(controlunit_module_1_reg_we),
    .dataOut(registers_module_1_dataout));  // open: clear
  assign ROM_TO_DATABUS_out = controlunit_module_1_wreg_re ? out_3 : 8'bz;  // Controlled_Buffer WREG_TO_DATABUS
  Clock clock_5 (.out(clock_5_out));
  assign ROM_TO_DATABUS_out = controlunit_module_1_rn_to_databus ? registers_module_1_dataout : 8'bz;  // Controlled_Buffer RN_TO_DATABUS
  assign controlled_buffer_5_out = keyboard_1_avail ? clock_5_out : 1'bz;  // Controlled_Buffer controlled_buffer_5
  Keyboard #(.buflen(8), .trigger("falling")) keyboard_1 (
    .clk(controlled_buffer_5_out), .avail(keyboard_1_avail), .data(out_4[6:0]));  // open: re, clr
  Clock clock_6 (.out(clock_6_out));
  ALU alu_1 (
    .ALUOP2(controlunit_module_1_alu_op[2]), .ALUOP1(controlunit_module_1_alu_op[1]),
    .ALUOP0(controlunit_module_1_alu_op[0]), .Wreg(out_3), .Rn(registers_module_1_dataout),
    .Result(alu_1_result), .carryF(alu_1_carryf), .zeroF(alu_1_zerof));
  D_Flip_Flop #(.trigger("high")) d_ff_1 (
    .D(alu_1_carryf), .clk(controlunit_module_1_alu_en), .Q(d_ff_1_q));  // open: Qn, preset, reset
  D_Flip_Flop #(.trigger("high")) d_ff_2 (
    .D(alu_1_zerof), .clk(controlunit_module_1_alu_en), .Q(d_ff_2_q));  // open: Qn, preset, reset
  assign ROM_TO_DATABUS_out = controlunit_module_1_ram_re ? out_1 : 8'bz;  // Controlled_Buffer controlled_buffer_6
  RAM_module ram_module_1 (
    .addr(out_2), .dataIn(out_3), .readEnable(controlunit_module_1_ram_re),
    .writeEnable(controlunit_module_1_ram_we), .clk(clock_6_out), .dataOut(out_1));
  assign ROM_TO_DATABUS_out = controlunit_module_1_alu_en ? alu_1_result : 8'bz;  // Controlled_Buffer ALU_ENABLE_CONTROLLER
  assign controlled_buffer_7_out = controlunit_module_1_out_en ? out_3 : 8'bz;  // Controlled_Buffer controlled_buffer_7
  Register register_1 (
    .D(controlled_buffer_7_out), .en(controlunit_module_1_out_en), .clk(clock_7_out), .Q(register_1_q));  // open: clr
  Register register_2 (
    .D(rom_module_1_data[7:0]), .en(controlunit_module_1_out_en), .clk(clock_7_out), .Q(register_2_q));  // open: clr
  Clock clock_7 (.out(clock_7_out));
  Register key (
    .D({1'b0, out_4[6:0]}), .en(controlunit_module_1_in_to_databus), .clk(clock_6_out), .Q(key_q));  // open: clr
  // DotMatrix #(.inputtype("select"), .matrixcols(8), .matrixrows(8)) dotmatrix_1: pin names not known; wires that end beside it: register_1_q, register_2_q
  assign ROM_TO_DATABUS_out = controlunit_module_1_in_to_databus ? key_q : 8'bz;  // Controlled_Buffer controlled_buffer_8

  assign out_4[7] = 1'b0;
  assign out_5 = out_4[6:0];

  // Notes on the sheet:
  //   DATABUS
  //   RAM TO DATABUS
  //   Key To Wreg
endmodule
